// Logisim project hw3.circ as structural Verilog: 5 circuits, main circuit SR_Latch
module SR_Latch (
  input  in_1,
  input  in_2,
  output out_3,
  output out_4
);

  wire or_1_out, or_2_out;

  or or_1 (or_1_out, in_1, out_4);
  or or_2 (or_2_out, out_3, in_2);
  not not_1 (out_3, or_1_out);
  not not_2 (out_4, or_2_out);

  // Notes on the sheet:
  //   Provided for you
endmodule

module D_Latch (
  input  in_1,
  input  in_2,
  output out_3
);

  wire and_1_out, and_2_out, not_1_out;

  not not_1 (not_1_out, in_1);
  and and_1 (and_1_out, in_1, in_2);
  and and_2 (and_2_out, not_1_out, in_2);
  SR_Latch SR (.in_1(and_1_out), .in_2(and_2_out), .out_4(out_3));  // open: out_3

  // Notes on the sheet:
  //   Strobe
  //   Provided for you
  //   We ignore the NOT Q output
endmodule

module Decoder (
  input  in_1,
  input  in_2,
  output out_3,
  output out_4,
  output out_5,
  output out_6
);

  wire not_1_out, not_2_out, not_3_out, not_4_out;

  not not_1 (not_1_out, in_1);
  not not_2 (not_2_out, in_2);
  not not_3 (not_3_out, in_1);
  not not_4 (not_4_out, in_2);
  and and_1 (out_3, not_1_out, not_2_out);
  and and_2 (out_4, not_3_out, in_2);
  and and_3 (out_5, in_1, not_4_out);
  and and_4 (out_6, in_1, in_2);

  // Notes on the sheet:
  //   Provided for you
endmodule

module RAM (
  input  in_1,
  input  _2Bit_Addr,
  input  in_3,
  input  _3Bit_Data,
  input  in_5,
  input  Write,
  output out_7,
  output _3_Bit_Out,
  output out_9,
  output out_10,
  output _3_Bit_Output,
  output out_12
);

  wire and_1_out, and_2_out, and_3_out, and_4_out, and_5_out, and_6_out, and_7_out, and_8_out, and_9_out,
       and_10_out, and_11_out, and_12_out, and_13_out, and_14_out, and_15_out, and_16_out, d_latch_1_out_3,
       d_latch_2_out_3, d_latch_3_out_3, d_latch_4_out_3, d_latch_5_out_3, d_latch_6_out_3, d_latch_7_out_3,
       d_latch_8_out_3, d_latch_9_out_3, d_latch_10_out_3, d_latch_11_out_3, d_latch_12_out_3,
       decoder_1_out_3, decoder_1_out_4, decoder_1_out_5, decoder_1_out_6;

  Decoder decoder_1 (
    .out_3(decoder_1_out_3), .out_4(decoder_1_out_4), .out_5(decoder_1_out_5), .out_6(decoder_1_out_6),
    .in_2(_2Bit_Addr), .in_1(in_1));
  D_Latch d_latch_1 (.out_3(d_latch_1_out_3), .in_2(and_1_out), .in_1(in_3));
  and and_1 (and_1_out, decoder_1_out_3, Write);
  D_Latch d_latch_2 (.out_3(d_latch_2_out_3), .in_2(and_2_out), .in_1(in_3));
  and and_2 (and_2_out, decoder_1_out_4, Write);
  D_Latch d_latch_3 (.out_3(d_latch_3_out_3), .in_2(and_3_out), .in_1(in_3));
  and and_3 (and_3_out, decoder_1_out_5, Write);
  D_Latch d_latch_4 (.out_3(d_latch_4_out_3), .in_2(and_4_out), .in_1(in_3));
  and and_4 (and_4_out, decoder_1_out_6, Write);
  and and_5 (and_5_out, d_latch_1_out_3, decoder_1_out_3);
  and and_6 (and_6_out, d_latch_2_out_3, decoder_1_out_4);
  and and_7 (and_7_out, d_latch_3_out_3, decoder_1_out_5);
  and and_8 (and_8_out, d_latch_4_out_3, decoder_1_out_6);
  or or_1 (out_9, and_5_out, and_6_out, and_7_out, and_8_out);
  D_Latch d_latch_5 (.out_3(d_latch_5_out_3), .in_2(and_1_out), .in_1(_3Bit_Data));
  D_Latch d_latch_6 (.out_3(d_latch_6_out_3), .in_2(and_2_out), .in_1(_3Bit_Data));
  D_Latch d_latch_7 (.out_3(d_latch_7_out_3), .in_2(and_3_out), .in_1(_3Bit_Data));
  D_Latch d_latch_8 (.out_3(d_latch_8_out_3), .in_2(and_4_out), .in_1(_3Bit_Data));
  and and_9 (and_9_out, d_latch_5_out_3, decoder_1_out_3);
  and and_10 (and_10_out, d_latch_6_out_3, decoder_1_out_4);
  and and_11 (and_11_out, d_latch_7_out_3, decoder_1_out_5);
  and and_12 (and_12_out, d_latch_8_out_3, decoder_1_out_6);
  or or_2 (_3_Bit_Output, and_9_out, and_10_out, and_11_out, and_12_out);
  D_Latch d_latch_9 (.out_3(d_latch_9_out_3), .in_2(and_1_out), .in_1(in_5));
  and and_13 (and_13_out, d_latch_9_out_3, decoder_1_out_3);
  D_Latch d_latch_10 (.out_3(d_latch_10_out_3), .in_2(and_2_out), .in_1(in_5));
  and and_14 (and_14_out, d_latch_10_out_3, decoder_1_out_4);
  D_Latch d_latch_11 (.out_3(d_latch_11_out_3), .in_2(and_3_out), .in_1(in_5));
  and and_15 (and_15_out, d_latch_11_out_3, in_5);
  D_Latch d_latch_12 (.out_3(d_latch_12_out_3), .in_2(and_4_out), .in_1(in_5));
  and and_16 (and_16_out, d_latch_12_out_3, decoder_1_out_6);
  or or_3 (out_12, and_13_out, and_14_out, and_15_out, and_16_out);

  // Notes on the sheet:
  //   Name: Tyler Seliber
  //   Implement  3 Bit, 4 Word RAM
  //   Implement the WRITE operation
  //   If you need help, look at slides 9-16 in week9.pdf
  //   Pledge: I pledge my honor that I have abided by the Stevens Honor System.
  //   The 3 Bit Output should reflect the values stored in the word selected by the 2Bit Addr
endmodule

module Remainder (
  input  in_1,
  input  in_2,
  input  in_3,
  input  in_4,
  input  in_5,
  output out_6,
  output out_7,
  output out_8
);

  wire _000_out, _001_out, _010_out, _011_out, _100_out, _101_out, _110_out, _111_out, _X_out, and_2_out,
       and_3_out, and_4_out, and_5_out, decoder_1_out_4, decoder_1_out_5, decoder_1_out_6, not_1_out,
       not_2_out, not_3_out, not_4_out, not_5_out, not_6_out, not_7_out, not_8_out, not_9_out, not_10_out,
       not_11_out, not_12_out, not_13_out, not_14_out, or_1_out, R00_out, R01_out, R10_out;

  not not_1 (not_1_out, in_1);
  not not_2 (not_2_out, in_2);
  not not_3 (not_3_out, in_3);
  not not_4 (not_4_out, in_1);
  not not_5 (not_5_out, in_3);
  Decoder decoder_1 (
    .out_3(out_8), .out_4(decoder_1_out_4), .out_5(decoder_1_out_5), .out_6(decoder_1_out_6), .in_2(in_5),
    .in_1(in_4));
  and _000 (_000_out, not_1_out, not_2_out, not_3_out);
  and _011 (_011_out, not_4_out, in_2, in_3);
  and _110 (_110_out, in_1, in_2, not_5_out);
  and _X (_X_out, in_3, decoder_1_out_5);
  or R00 (R00_out, _000_out, _011_out, _110_out);
  // AND_Gate and_1 has open pins: in0=decoder_1_out_6, in1=R00_out, out=open
  or or_1 (or_1_out, out_8, decoder_1_out_5, decoder_1_out_6);
  not not_6 (not_6_out, in_1);
  not not_7 (not_7_out, in_2);
  not not_8 (not_8_out, in_2);
  not not_9 (not_9_out, in_3);
  not not_10 (not_10_out, in_1);
  and _010 (_010_out, not_10_out, in_2, not_11_out);
  not not_11 (not_11_out, in_3);
  and _101 (_101_out, in_1, not_12_out, in_3);
  not not_12 (not_12_out, in_2);
  not not_13 (not_13_out, or_1_out);
  and and_2 (and_2_out, not_13_out, decoder_1_out_4);
  and _001 (_001_out, not_6_out, not_7_out, in_3);
  or R10 (R10_out, _001_out, _100_out, _111_out);
  and _100 (_100_out, in_1, not_8_out, not_9_out);
  and _111 (_111_out, in_1, in_2, in_3);
  and and_3 (and_3_out, decoder_1_out_6, R10_out);
  or R01 (R01_out, _010_out, _101_out);
  not not_14 (not_14_out, and_2_out);
  and and_4 (and_4_out, decoder_1_out_6, R01_out);
  and and_5 (and_5_out, not_14_out, decoder_1_out_4);
  or or_2 (out_6, and_5_out, and_3_out);
  or or_3 (out_7, and_5_out, _X_out, and_4_out);

  // Notes on the sheet:
  //   Numerator
  //   Divisor
  //   Part 2: Create a circuit to calculate remainders, given a 3-bit numerator and 2-bit divisor.
  //   (Hint: You may want to write a truth table first)
  //   Remainder
  //   Error bit (Set when division isn't possible)
endmodule
