// Logisim project lab8.circ as structural Verilog: 3 circuits, main circuit XOR
module XOR (
  input  X,
  input  Y,
  output out_3
);

  wire and_1_out, and_2_out, not_1_out, not_2_out;

  not not_1 (not_1_out, X);
  and and_1 (and_1_out, not_1_out, Y);
  or or_1 (out_3, and_1_out, and_2_out);
  not not_2 (not_2_out, Y);
  and and_2 (and_2_out, X, not_2_out);

  // Notes on the sheet:
  //   Use minterm expansion to create an XOR gate using AND + OR gates
endmodule

module ParityGenerator (
  input  X,
  input  Y,
  input  Z,
  output Parity
);

  wire and_1_out, Just1_2_parity, Just1_3_parity, Just1_parity, XOR_2_out_3, XOR_out_3;

  Just1 Just1 (.X(X), .Y(Y), .Z(Z), .Parity(Just1_parity));
  XOR XOR (.out_3(XOR_out_3), .Y(Just1_2_parity), .X(Just1_parity));
  Just1 Just1_2 (.X(Y), .Y(X), .Z(Z), .Parity(Just1_2_parity));
  Just1 Just1_3 (.X(Z), .Y(X), .Z(Y), .Parity(Just1_3_parity));
  XOR XOR_2 (.out_3(XOR_2_out_3), .Y(Just1_3_parity), .X(XOR_out_3));
  and and_1 (and_1_out, X, Y, Z);
  or or_1 (Parity, XOR_2_out_3, and_1_out);

  // Notes on the sheet:
  //   Input Bits
  //   Output Bit
  //   Write your parity circuit here
  //   the output = 1 if an odd number of inputs (1 or 3) are 1, otherwise 0
  //   ONLY use: NOT, AND, OR, and any custom functions you write (included in the .circ submission)
  //   Tyler Seliber
  //   I pledge my honor that I have abided by the Stevens Honor System.
endmodule

module Just1 (
  input  X,
  input  Y,
  input  Z,
  output Parity
);

  wire and_2_out, not_1_out, not_2_out;

  not not_1 (not_1_out, Y);
  and and_1 (Parity, X, and_2_out);
  not not_2 (not_2_out, Z);
  and and_2 (and_2_out, not_1_out, not_2_out);

  // Notes on the sheet:
  //   Output Bit
  //   Returns 1 if and only if the first argument is 1 and the other two are 0.
endmodule
